# Fritzing sketch Alarma (saved by Fritzing 0.9.3b)
breadboards: 1

parts:
  Componente1 = Arduino Uno (Rev3)
  LED1 = smd LED [color="Red (633nm)" package="0603 [SMD]"]
  R1 = Resistor [tolerance=±5% resistance=330 package=THT]
  J1 = Piezo Speaker
  S1 = Reed switch [package=THT]

nets:
  N1: Componente1.D9_PWM, J1.pin2
  N2: Componente1.D13/SCK, R1.Pin_0
  N3: Componente1.D5_PWM, S1.pin_2
  N4: Componente1.GND, LED1.anode, J1.pin1, S1.pin_1
  N5: LED1.cathode, R1.Pin_1
